# Fritzing sketch Fermentor (saved by Fritzing 1.0.3b)

parts:
  Part1 = Arduino Uno (Rev3) - ICSP
  Part2 = OLED Monochrome 128x32 I2C [part_number=931]
  JACK1 = 2.1mm Barrel Jack with Terminal Block
  DC1 = DC_DC_XL4016 [package=board_screw]
  J1 = Camdenboss CTB0158-5 [part_number=CTB0158-5 package=THT]
  J2 = Camdenboss CTB0158-3 [part_number=CTB0158-3 package=THT]
  AM1 = AM2302 Humidity and Temperature Sensor

nets:
  N1: Part1.A4/SDA, Part2.SDA
  N2: Part1.A5/SCL, Part2.SCL
  N3: Part1.D8, AM1.DATA
  N4: Part1.D10_PWM/SS, J2.terminal_3
  N5: Part1.D11_PWM/MOSI, J2.terminal_2
  GND: Part1.GND, Part2.GND, DC1.OUT-, J1.terminal_5, J2.terminal_1, AM1.GND
  N6: Part1.D2, Part2.RESET
  N7: Part1.D4, J1.terminal_4
  N8: Part1.D5_PWM, J1.terminal_3
  N9: Part1.D6_PWM, J1.terminal_2
  N10: Part1.D7, J1.terminal_1
  5V: Part1.5V, Part2.VIN, AM1.VDD
  N11: Part1.VIN, DC1.OUT+
  N12: JACK1.POS, DC1.IN+
  N13: JACK1.NEG, DC1.IN-

custom parts:
  OLED Monochrome 128x32 I2C: These displays are small, only about 1" diagonal, but very readable due to the high contrast of an OLED display. This display is made of 128x32 individual white OLED pixels, each one is turned on or off by the controller chip. Because the display makes its own light, no backlight is required. This reduces the power required to run the OLED and is why the display has such high contrast; we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
